# Fritzing sketch Model (saved by Fritzing 0.9.3b)
breadboards: 1

parts:
  KY-1 = Keyes Relay [package=THT]
  LED2 = LEDs [package=led10mm]
  Part1 = Arduino Yun
  VCC1 = 4 x AAA Battery Mount
  R1 = Resistor [tolerance=±5% resistance=220 package=THT]
  IR_Sensor_Switch1 = Infrared Sensor Switch
  IR_Sensor_Switch2 = Infrared Sensor Switch

nets:
  N1: KY-1.signal, Part1.D8
  VCC: KY-1.power, KY-1.C, Part1.5V, IR_Sensor_Switch1.Vcc, IR_Sensor_Switch2.Vcc
  GND: KY-1.ground, LED2.C, Part1.GND, VCC1.-, IR_Sensor_Switch1.GND, IR_Sensor_Switch2.GND
  N2: KY-1.NO, R1.Pin_0
  N3: LED2.A, R1.Pin_1
  N4: Part1.D12/MISO, IR_Sensor_Switch2.OUT
  N5: Part1.D13/SCK, IR_Sensor_Switch1.OUT
  N6: Part1.VIN, VCC1.+

custom parts:
  Keyes Relay: The Keyes 5V relay module is suitable for SCM development, home appliance control. It uses a 5V~12V TIL control signal which can control DC / AC signal.
  Infrared Sensor Switch: - Working voltage: DC 5V - Working current: 10~15mA - Detecting range: 3~80cm (adjustable) - Red: VCC, Green: GND, Yellow: OUT
